# Fritzing sketch fritz (saved by Fritzing 0.9.1b)
breadboards: 1

parts:
  Part1 = Arduino Uno (Rev3)
  U1 = POT [package=pot_mammoth]
  LED2 = smd LED [color="Red (633nm)" package="0805 [SMD]"]
  R1 = Resistor [tolerance=±5% resistance=220 package="1206 [SMD]"]

nets:
  N1: Part1.A0, U1.A
  N2: Part1.D9_PWM, LED2.anode
  N3: Part1.5V, U1.E
  N4: Part1.GND, U1.S, R1.Pin_0
  N5: LED2.cathode, R1.Pin_1
